// Logisim project CSC220Project.circ as structural Verilog: 1 circuit, main circuit main
module main (
  input  [3:0] S3S2S1S0,
  input  [7:0] X,
  input  [7:0] Y,
  output V,
  output N,
  output C,
  output Z,
  output [7:0] G
);

  wire and_2_out, and_3_out, not_2_out, not_3_out, not_4_out;
  wire [6:0] adder_1_out;
  wire [7:0] and_1_out, multiplexer_1_out, multiplexer_2_out, nand_1_out, not_1_out, xor_1_out;

  assign not_1_out = ~Y;  // NOT_Gate not_1, 8 bits wide
  assign and_1_out = X & not_1_out;  // AND_Gate and_1, 8 bits wide
  assign xor_1_out = X ^ Y;  // XOR_Gate xor_1, 8 bits wide
  assign nand_1_out = ~(X & Y);  // NAND_Gate nand_1, 8 bits wide
  Multiplexer #(.select(2), .width(8), .enable("false")) multiplexer_1 (
    .in0(X), .in1(not_1_out), .in2({8{1'b0}}), .in3(8'h2), .out(multiplexer_1_out), .sel(S3S2S1S0[2:1]));
  Adder adder_1 (.a(X), .b(multiplexer_1_out), .out({N, adder_1_out}), .cin(S3S2S1S0[0]), .cout(C));
  Multiplexer #(.select(3), .width(8), .enable("false")) multiplexer_2 (
    .in0(xor_1_out), .in1(and_1_out), .in2(nand_1_out), .in3(X), .in4(Y), .in5({1'b0, Y[7:1]}),
    .in6({Y[6:0], Y[7]}), .in7({{2{Y[7]}}, Y[6:1]}), .out(multiplexer_2_out), .sel(S3S2S1S0[2:0]));
  Multiplexer #(.width(8), .enable("false")) multiplexer_3 (
    .in0({N, adder_1_out}), .in1(multiplexer_2_out), .out(G), .sel(S3S2S1S0[3]));
  not not_2 (not_2_out, X[7]);
  not not_3 (not_3_out, multiplexer_1_out[7]);
  not not_4 (not_4_out, N);
  and and_2 (and_2_out, not_2_out, N, not_3_out);
  and and_3 (and_3_out, X[7], not_4_out, multiplexer_1_out[7]);
  or or_1 (V, and_2_out, and_3_out);
  nor nor_1 (Z, G[0], G[1], G[2], G[3], G[4], G[5], G[6], G[7]);

  // Notes on the sheet:
  //   Logical Shift Right Y
  //   Circular Shift Left Y 
  //   Arthimetic Shift Right Y
endmodule
